// Logisim project Calculator.circ as structural Verilog: 1 circuit, main circuit main
module main (
  input  _0,
  input  _1,
  input  _2,
  input  _3,
  input  _4,
  input  _5,
  input  _6,
  input  _7,
  input  _8,
  input  _9,
  input  A,
  input  B,
  input  C,
  input  D,
  input  E,
  input  F,
  input  in_17,
  input  _0_2,
  input  _1_2,
  input  _2_2,
  input  _3_2,
  input  _4_2,
  input  _5_2,
  input  _6_2,
  input  _7_2,
  input  _8_2,
  input  _9_2,
  input  A_2,
  input  B_2,
  input  C_2,
  input  D_2,
  input  E_2,
  input  F_2,
  output [3:0] out_34,
  output [3:0] out_35,
  output [4:0] out_36
);

  Soma_main main_1 (
    ._0(_0_2), ._0_2(_0), ._1(_1_2), ._1_2(_1), ._2(_2_2), ._2_2(_2), ._3(_3_2), ._3_2(_3), ._4(_4_2),
    ._4_2(_4), ._5(_5_2), ._5_2(_5), ._6(_6_2), ._6_2(_6), ._7(_7_2), ._7_2(_7), ._8(_8_2), ._8_2(_8),
    ._9(_9_2), ._9_2(_9), .A(A_2), .A_2(A), .B(B_2), .B_2(B), .C(C_2), .C_2(C), .D(D_2), .D_2(D), .E(E_2),
    .E_2(E), .F(F_2), .F_2(F), .out_33({out_36[4], out_35}));
  \Subtração_main  main_2 (
    ._0B(_0), ._0(_0_2), ._1B(_1), ._1(_1_2), ._2B(_2), ._2(_2_2), ._3B(_3), ._3(_3_2), ._4B(_4), ._4(_4_2),
    ._5B(_5), ._5(_5_2), ._6B(_6), ._6(_6_2), ._7B(_7), ._7(_7_2), ._8B(_8), ._8(_8_2), ._9B(_9), ._9(_9_2),
    .AB(A), .A(A_2), .BB(B), .B(B_2), .CB(C), .C(C_2), .DB(D), .D(D_2), .EB(E), .E(E_2), .FB(F), .F(F_2),
    .out_33(out_34));
  Hex_Digit_Display hex_digit_display_1 (.value({{3{in_17}}, out_36[4]}));  // open: dp
  Hex_Digit_Display hex_digit_display_2 (.value(out_35));  // open: dp
  // AND_Gate and_1 is placed but not wired

  assign out_36[3:0] = out_35;

  // Notes on the sheet:
  //   ENTRADA B (2)
  //   ENTRADA A (1)
endmodule
